# Fritzing sketch pcb_sketch (saved by Fritzing 0.9.9b)
perfboards: 1

parts:
  J1 = female pin header, 8 pins [form="♀ (female)"]
  J2 = female pin header, 8 pins [form="♀ (female)"]  # not connected
  HC-SR04_Sensor_1 = HC-SR04 Ultrasonic Distance Sensor
  R1 = Resistor [tolerance=±5% power=0.25 resistance=220 package=THT]
  R2 = Resistor [tolerance=±5% power=0.25 resistance=220 package=THT]
  R3 = Resistor [tolerance=±5% power=0.25 resistance=220 package=THT]
  J3 = Piezo Speaker
  J4 = male pin header, 4 pins [form="♂ (male)"]  # not connected
  S1 = Pushbutton [package="[THT]"]

nets:
  N1: J1.pin8, HC-SR04_Sensor_1.VCC
  N2: HC-SR04_Sensor_1.GND, J3.pin2
  N3: R1.Pin_0, R2.Pin_1
  N4: R2.Pin_0, R3.Pin_1
  N5: S1.Pin_1, S1.Pin_2
  N6: S1.Pin_3, S1.Pin_4
